// Logisim project nibbleOperator.circ as structural Verilog: 24 circuits, main circuit CPU
module ALU (
  input  in_1,
  input  in_2,
  input  in_3,
  input  in_4,
  input  ZwR,
  input  SIn,
  input  RegIn,
  input  RSh,
  input  Sub,
  input  Inc,
  input  AddCF,
  input  CF,
  input  Op1,
  input  Op2,
  input  Op3,
  input  ZF,
  input  Save,
  input  Out,
  output CF_2,
  output ZF_2,
  output out_21,
  output out_22,
  output out_23,
  output out_24
);

  wire and_1_out, and_2_out, and_3_out, and_4_out, and_5_out, and_6_out, and_7_out, and_8_out, and_9_out,
       and_10_out, and_11_out, and_12_out, and_13_out, and_14_out, and_15_out, and_16_out, and_17_out,
       and_18_out, and_19_out, and_20_out, and_21_out, and_22_out, and_23_out, and_24_out, and_25_out,
       and_26_out, and_27_out, and_28_out, and_29_out, controlled_buffer_4_out, d_ff_1_q, d_ff_2_q, d_ff_3_q,
       d_ff_4_q, d_ff_5_q, d_ff_6_q, d_ff_8_q, d_ff_9_q, or_1_out, or_2_out, or_3_out, or_4_out, or_5_out,
       or_6_out, or_7_out, or_8_out, or_9_out, or_10_out, or_11_out, or_12_out, or_13_out,
       undsteuerleitung_1_out_6, undsteuerleitung_1_out_7, undsteuerleitung_1_out_8,
       undsteuerleitung_1_out_9, undsteuerleitung_2_out_6, undsteuerleitung_2_out_7,
       undsteuerleitung_2_out_8, undsteuerleitung_2_out_9, undsteuerleitung_3_out_6,
       undsteuerleitung_3_out_7, undsteuerleitung_3_out_8, undsteuerleitung_3_out_9,
       undsteuerleitung_4_out_6, undsteuerleitung_4_out_7, undsteuerleitung_4_out_8,
       undsteuerleitung_4_out_9, undsteuerleitung_5_out_6, undsteuerleitung_5_out_7,
       undsteuerleitung_5_out_8, undsteuerleitung_5_out_9, volladdierer_1_out_4, volladdierer_1_out_5,
       volladdierer_2_out_4, volladdierer_2_out_5, volladdierer_3_out_4, volladdierer_3_out_5,
       volladdierer_4_out_4, volladdierer_4_out_5, xor_1_out, xor_2_out, xor_3_out, xor_4_out, xor_5_out,
       xor_6_out, xor_7_out, xor_8_out;

  xor xor_1 (xor_1_out, and_6_out, and_13_out);
  undSteuerleitung undsteuerleitung_1 (
    .in_1(xor_1_out), .in_2(xor_2_out), .in_3(xor_3_out), .in_4(xor_4_out), .Stleitung(and_1_out),
    .out_6(undsteuerleitung_1_out_6), .out_7(undsteuerleitung_1_out_7), .out_8(undsteuerleitung_1_out_8),
    .out_9(undsteuerleitung_1_out_9));
  xor xor_2 (xor_2_out, and_7_out, and_15_out);
  and and_1 (and_1_out, Op1, Op2, Op3);
  and and_2 (and_2_out, Op1, Op2, ~Op3);  // AND_Gate
  xor xor_3 (xor_3_out, and_8_out, and_16_out);
  xor xor_4 (xor_4_out, and_11_out, and_17_out);
  and and_3 (and_3_out, Op1, ~Op2, Op3);  // AND_Gate
  and and_4 (and_4_out, Op1, ~Op2, ~Op3);  // AND_Gate
  or or_1 (or_1_out, and_6_out, and_13_out);
  or or_2 (or_2_out, and_7_out, and_15_out);
  undSteuerleitung undsteuerleitung_2 (
    .in_1(or_1_out), .in_2(or_2_out), .in_3(or_4_out), .in_4(or_3_out), .Stleitung(and_2_out),
    .out_6(undsteuerleitung_2_out_6), .out_7(undsteuerleitung_2_out_7), .out_8(undsteuerleitung_2_out_8),
    .out_9(undsteuerleitung_2_out_9));
  and and_5 (and_5_out, ~Op1, Op2, Op3);  // AND_Gate
  D_Flip_Flop d_ff_1 (.clk(ZwR), .D(in_1), .Q(d_ff_1_q));  // open: Qn, preset, en, reset
  and and_6 (and_6_out, RegIn, d_ff_1_q);
  or or_3 (or_3_out, and_11_out, and_17_out);
  or or_4 (or_4_out, and_8_out, and_16_out);
  D_Flip_Flop d_ff_2 (.clk(ZwR), .D(in_2), .Q(d_ff_2_q));  // open: Qn, preset, en, reset
  and and_7 (and_7_out, RegIn, d_ff_2_q);
  D_Flip_Flop d_ff_3 (.clk(ZwR), .D(in_3), .Q(d_ff_3_q));  // open: Qn, preset, en, reset
  and and_8 (and_8_out, RegIn, d_ff_3_q);
  and and_9 (and_9_out, and_7_out, and_15_out);
  and and_10 (and_10_out, and_6_out, and_13_out);
  undSteuerleitung undsteuerleitung_3 (
    .in_1(and_10_out), .in_2(and_9_out), .in_3(and_12_out), .in_4(and_14_out), .Stleitung(and_3_out),
    .out_6(undsteuerleitung_3_out_6), .out_7(undsteuerleitung_3_out_7), .out_8(undsteuerleitung_3_out_8),
    .out_9(undsteuerleitung_3_out_9));
  or or_5 (or_5_out, undsteuerleitung_1_out_6, undsteuerleitung_2_out_6, undsteuerleitung_5_out_6, undsteuerleitung_3_out_6, undsteuerleitung_4_out_6);
  D_Flip_Flop d_ff_4 (.clk(ZwR), .D(in_4), .Q(d_ff_4_q));  // open: Qn, preset, en, reset
  and and_11 (and_11_out, RegIn, d_ff_4_q);
  and and_12 (and_12_out, and_8_out, and_16_out);
  or or_6 (or_6_out, undsteuerleitung_1_out_7, undsteuerleitung_2_out_7, undsteuerleitung_5_out_7, undsteuerleitung_3_out_7, undsteuerleitung_4_out_7);
  D_Flip_Flop d_ff_5 (.clk(Save), .D(or_5_out), .Q(d_ff_5_q));  // open: Qn, preset, en, reset
  assign out_21 = Out ? d_ff_5_q : 1'bz;  // Controlled_Buffer controlled_buffer_1
  and and_13 (and_13_out, in_1, SIn);
  and and_14 (and_14_out, and_11_out, and_17_out);
  or or_7 (or_7_out, undsteuerleitung_1_out_8, undsteuerleitung_2_out_8, undsteuerleitung_5_out_8, undsteuerleitung_3_out_8, undsteuerleitung_4_out_8);
  D_Flip_Flop d_ff_6 (.clk(Save), .D(or_6_out), .Q(d_ff_6_q));  // open: Qn, preset, en, reset
  assign out_22 = Out ? d_ff_6_q : 1'bz;  // Controlled_Buffer controlled_buffer_2
  and and_15 (and_15_out, in_2, SIn);
  and and_16 (and_16_out, in_3, SIn);
  D_Flip_Flop d_ff_7 (.clk(CF), .D(controlled_buffer_4_out), .Q(CF_2));  // open: Qn, preset, en, reset
  or or_8 (or_8_out, undsteuerleitung_1_out_9, undsteuerleitung_2_out_9, undsteuerleitung_5_out_9, undsteuerleitung_3_out_9, undsteuerleitung_4_out_9);
  D_Flip_Flop d_ff_8 (.clk(Save), .D(or_7_out), .Q(d_ff_8_q));  // open: Qn, preset, en, reset
  assign out_23 = Out ? d_ff_8_q : 1'bz;  // Controlled_Buffer controlled_buffer_3
  and and_17 (and_17_out, in_4, SIn);
  assign controlled_buffer_4_out = and_4_out ? volladdierer_2_out_5 : 1'bz;  // Controlled_Buffer controlled_buffer_4
  D_Flip_Flop d_ff_9 (.clk(Save), .D(or_8_out), .Q(d_ff_9_q));  // open: Qn, preset, en, reset
  assign out_24 = Out ? d_ff_9_q : 1'bz;  // Controlled_Buffer controlled_buffer_5
  xor xor_5 (xor_5_out, and_13_out, Sub);
  vollAddierer volladdierer_1 (
    .in_1(and_7_out), .in_2(xor_6_out), .in_3(volladdierer_3_out_5), .out_5(volladdierer_1_out_5),
    .out_4(volladdierer_1_out_4));
  vollAddierer volladdierer_2 (
    .in_1(and_6_out), .in_2(xor_5_out), .in_3(volladdierer_1_out_5), .out_5(volladdierer_2_out_5),
    .out_4(volladdierer_2_out_4));
  undSteuerleitung undsteuerleitung_4 (
    .in_1(volladdierer_2_out_4), .in_2(volladdierer_1_out_4), .in_3(volladdierer_3_out_4),
    .in_4(volladdierer_4_out_4), .Stleitung(and_4_out), .out_6(undsteuerleitung_4_out_6),
    .out_7(undsteuerleitung_4_out_7), .out_8(undsteuerleitung_4_out_8), .out_9(undsteuerleitung_4_out_9));
  and and_18 (and_18_out, ~or_5_out, ~or_6_out, ~or_7_out, ~or_8_out);  // AND_Gate
  xor xor_6 (xor_6_out, and_15_out, Sub);
  xor xor_7 (xor_7_out, and_16_out, Sub);
  vollAddierer volladdierer_3 (
    .in_1(and_8_out), .in_2(xor_7_out), .in_3(volladdierer_4_out_5), .out_5(volladdierer_3_out_5),
    .out_4(volladdierer_3_out_4));
  D_Flip_Flop d_ff_10 (.clk(ZF), .D(and_18_out), .Q(ZF_2));  // open: Qn, preset, en, reset
  xor xor_8 (xor_8_out, and_17_out, Sub);
  or or_9 (or_9_out, Inc, and_19_out);
  vollAddierer volladdierer_4 (
    .in_1(and_11_out), .in_2(xor_8_out), .in_3(or_9_out), .out_5(volladdierer_4_out_5),
    .out_4(volladdierer_4_out_4));
  and and_19 (and_19_out, AddCF, CF_2);
  and and_20 (and_20_out, and_13_out, ~RSh);  // AND_Gate
  and and_21 (and_21_out, and_5_out, ~RSh);  // AND_Gate
  assign controlled_buffer_4_out = and_21_out ? and_20_out : 1'bz;  // Controlled_Buffer controlled_buffer_6
  and and_22 (and_22_out, and_15_out, ~RSh);  // AND_Gate
  and and_23 (and_23_out, and_13_out, RSh);
  or or_10 (or_10_out, and_22_out, 1'b0);
  or or_11 (or_11_out, and_26_out, and_23_out);
  undSteuerleitung undsteuerleitung_5 (
    .in_1(or_10_out), .in_2(or_11_out), .in_3(or_12_out), .in_4(or_13_out), .Stleitung(and_5_out),
    .out_6(undsteuerleitung_5_out_6), .out_7(undsteuerleitung_5_out_7), .out_8(undsteuerleitung_5_out_8),
    .out_9(undsteuerleitung_5_out_9));
  and and_24 (and_24_out, and_16_out, RSh);
  and and_25 (and_25_out, and_15_out, RSh);
  and and_26 (and_26_out, and_16_out, ~RSh);  // AND_Gate
  or or_12 (or_12_out, and_27_out, and_25_out);
  and and_27 (and_27_out, and_17_out, ~RSh);  // AND_Gate
  and and_28 (and_28_out, and_17_out, RSh);
  assign controlled_buffer_4_out = and_29_out ? and_28_out : 1'bz;  // Controlled_Buffer controlled_buffer_7
  or or_13 (or_13_out, 1'b0, and_24_out);
  and and_29 (and_29_out, RSh, and_5_out);
endmodule

// undSt
module undSteuerleitung (
  input  in_1,
  input  in_2,
  input  in_3,
  input  in_4,
  input  Stleitung,
  output out_6,
  output out_7,
  output out_8,
  output out_9
);

  and and_1 (out_6, in_1, Stleitung);
  and and_2 (out_7, in_2, Stleitung);
  and and_3 (out_8, in_3, Stleitung);
  and and_4 (out_9, in_4, Stleitung);
endmodule

// VA
module vollAddierer (
  input  in_1,
  input  in_2,
  input  in_3,
  output out_4,
  output out_5
);

  wire and_1_out, and_2_out, and_3_out, and_4_out, xor_1_out, xor_2_out;

  and and_1 (and_1_out, in_1, in_2, in_3);
  and and_2 (and_2_out, in_1, in_2);
  ExactlyOne xor_1 (.out(xor_1_out), .in0(and_2_out), .in1(and_4_out), .in2(and_3_out));
  or or_1 (out_5, and_1_out, xor_1_out);
  and and_3 (and_3_out, in_2, in_3);
  and and_4 (and_4_out, in_1, in_3);
  or or_2 (out_4, and_1_out, xor_2_out);
  ExactlyOne xor_2 (.out(xor_2_out), .in0(in_1), .in1(in_2), .in2(in_3));
endmodule

module CPU (
  input  in_1,
  input  in_2,
  input  in_3,
  input  in_4,
  output out_5,
  output out_6,
  output out_7,
  output out_8,
  output out_9,
  output out_10,
  output out_11,
  output out_12,
  output out_13,
  output out_14,
  output out_15,
  output out_16
);

  wire addresswerk_1_out_24, addresswerk_1_out_25, addresswerk_1_out_26, addresswerk_1_out_27,
       addresswerk_1_out_28, addresswerk_1_out_29, addresswerk_1_out_30, addresswerk_1_out_31, alu_1_out_21,
       alu_1_out_22, alu_1_out_23, alu_1_out_24, clock_1_out, steuerwerk_1_addresswerk, steuerwerk_1_alu,
       steuerwerk_1_biu, steuerwerk_1_out_7, steuerwerk_1_out_8, steuerwerk_1_out_9, steuerwerk_1_out_10,
       steuerwerk_1_out_11, steuerwerk_1_out_12, steuerwerk_1_out_13, steuerwerk_1_out_15,
       steuerwerk_1_out_16, steuerwerk_1_out_17, steuerwerk_1_out_18, steuerwerk_1_out_20,
       steuerwerk_1_out_21, steuerwerk_1_out_22, steuerwerk_1_out_23, steuerwerk_1_out_24,
       steuerwerk_1_out_25, steuerwerk_1_out_26, steuerwerk_1_out_27, steuerwerk_1_out_28,
       steuerwerk_1_out_29, steuerwerk_1_out_30, steuerwerk_1_out_31, steuerwerk_1_out_32,
       steuerwerk_1_out_33, steuerwerk_1_out_34, steuerwerk_1_out_35, steuerwerk_1_out_36,
       steuerwerk_1_out_37, steuerwerk_1_out_39, steuerwerk_1_out_40, steuerwerk_1_out_41,
       steuerwerk_1_out_42, steuerwerk_1_out_43, steuerwerk_1_out_44, steuerwerk_1_out_45,
       steuerwerk_1_out_46, steuerwerk_1_out_47, steuerwerk_1_out_48, steuerwerk_1_out_49,
       steuerwerk_1_out_50, steuerwerk_1_out_51, steuerwerk_1_registersatz;

  Clock clock_1 (.out(clock_1_out));
  Steuerwerk steuerwerk_1 (
    .Takt(clock_1_out), .in_1(alu_1_out_21), .in_2(alu_1_out_22), .in_3(alu_1_out_23), .in_4(alu_1_out_24),
    .BIU(steuerwerk_1_biu), .out_7(steuerwerk_1_out_7), .out_8(steuerwerk_1_out_8),
    .out_9(steuerwerk_1_out_9), .out_10(steuerwerk_1_out_10), .out_11(steuerwerk_1_out_11),
    .out_12(steuerwerk_1_out_12), .out_13(steuerwerk_1_out_13), .Registersatz(steuerwerk_1_registersatz),
    .out_15(steuerwerk_1_out_15), .out_16(steuerwerk_1_out_16), .out_17(steuerwerk_1_out_17),
    .out_18(steuerwerk_1_out_18), .Addresswerk(steuerwerk_1_addresswerk), .out_20(steuerwerk_1_out_20),
    .out_21(steuerwerk_1_out_21), .out_22(steuerwerk_1_out_22), .out_23(steuerwerk_1_out_23),
    .out_24(steuerwerk_1_out_24), .out_25(steuerwerk_1_out_25), .out_26(steuerwerk_1_out_26),
    .out_27(steuerwerk_1_out_27), .out_28(steuerwerk_1_out_28), .out_29(steuerwerk_1_out_29),
    .out_30(steuerwerk_1_out_30), .out_31(steuerwerk_1_out_31), .out_32(steuerwerk_1_out_32),
    .out_33(steuerwerk_1_out_33), .out_34(steuerwerk_1_out_34), .out_35(steuerwerk_1_out_35),
    .out_36(steuerwerk_1_out_36), .out_37(steuerwerk_1_out_37), .ALU(steuerwerk_1_alu),
    .out_39(steuerwerk_1_out_39), .out_40(steuerwerk_1_out_40), .out_41(steuerwerk_1_out_41),
    .out_42(steuerwerk_1_out_42), .out_43(steuerwerk_1_out_43), .out_44(steuerwerk_1_out_44),
    .out_45(steuerwerk_1_out_45), .out_46(steuerwerk_1_out_46), .out_47(steuerwerk_1_out_47),
    .out_48(steuerwerk_1_out_48), .out_49(steuerwerk_1_out_49), .out_50(steuerwerk_1_out_50),
    .out_51(steuerwerk_1_out_51));
  Addresswerk addresswerk_1 (
    .CSIn(steuerwerk_1_addresswerk), .CSOut(steuerwerk_1_out_20), .IPExtIn(steuerwerk_1_out_21),
    .IPIn(steuerwerk_1_out_22), .IPInc(steuerwerk_1_out_23), .DSIn(steuerwerk_1_out_24),
    .DSOut(steuerwerk_1_out_25), .SIIn(steuerwerk_1_out_26), .ESIn(steuerwerk_1_out_27),
    .ESOut(steuerwerk_1_out_28), .DIIn(steuerwerk_1_out_29), .SSIn(steuerwerk_1_out_30),
    .BPIn(steuerwerk_1_out_31), .SSBPOut(steuerwerk_1_out_32), .SPExtIn(steuerwerk_1_out_33),
    .SPIn(steuerwerk_1_out_34), .SPInc(steuerwerk_1_out_35), .SPDec(steuerwerk_1_out_36),
    .SSSPOut(steuerwerk_1_out_37), .in_1(alu_1_out_21), .in_2(alu_1_out_22), .in_3(alu_1_out_23),
    .in_4(alu_1_out_24), .out_24(addresswerk_1_out_24), .out_25(addresswerk_1_out_25),
    .out_26(addresswerk_1_out_26), .out_27(addresswerk_1_out_27), .out_28(addresswerk_1_out_28),
    .out_29(addresswerk_1_out_29), .out_30(addresswerk_1_out_30), .out_31(addresswerk_1_out_31));
  ALU alu_1 (
    .ZwR(steuerwerk_1_alu), .SIn(steuerwerk_1_out_39), .RegIn(steuerwerk_1_out_40),
    .RSh(steuerwerk_1_out_41), .Sub(steuerwerk_1_out_42), .Inc(steuerwerk_1_out_43),
    .AddCF(steuerwerk_1_out_44), .CF(steuerwerk_1_out_45), .Op1(steuerwerk_1_out_46),
    .Op2(steuerwerk_1_out_47), .Op3(steuerwerk_1_out_48), .ZF(steuerwerk_1_out_49),
    .Save(steuerwerk_1_out_50), .Out(steuerwerk_1_out_51), .in_1(alu_1_out_21), .in_2(alu_1_out_22),
    .in_3(alu_1_out_23), .in_4(alu_1_out_24), .out_21(alu_1_out_21), .out_22(alu_1_out_22),
    .out_23(alu_1_out_23), .out_24(alu_1_out_24));  // open: CF_2, ZF_2
  Registersatz registersatz_1 (
    .In(steuerwerk_1_registersatz), .Out(steuerwerk_1_out_15), .St1(steuerwerk_1_out_16),
    .St2(steuerwerk_1_out_17), .St3(steuerwerk_1_out_18), .in_2(alu_1_out_21), .in_3(alu_1_out_22),
    .in_4(alu_1_out_23), .in_5(alu_1_out_24), .out_10(alu_1_out_21), .out_11(alu_1_out_22),
    .out_12(alu_1_out_23), .out_13(alu_1_out_24));
  BIU biu_1 (
    .In(steuerwerk_1_biu), .G(steuerwerk_1_out_7), .Dir(steuerwerk_1_out_8), .Out1(steuerwerk_1_out_9),
    .Out2(steuerwerk_1_out_10), .In_13(steuerwerk_1_out_11), .G_2(steuerwerk_1_out_12),
    .Out1_2(steuerwerk_1_out_13), .out_25(alu_1_out_21), .out_26(alu_1_out_22), .out_27(alu_1_out_23),
    .out_28(alu_1_out_24), .in_1(alu_1_out_21), .in_2(alu_1_out_22), .in_3(alu_1_out_23),
    .in_4(alu_1_out_24), .in_5(addresswerk_1_out_24), .in_6(addresswerk_1_out_25),
    .in_7(addresswerk_1_out_26), .in_8(addresswerk_1_out_27), .in_9(addresswerk_1_out_28),
    .in_10(addresswerk_1_out_29), .in_11(addresswerk_1_out_30), .in_12(addresswerk_1_out_31),
    .out_29(out_16), .out_30(out_15), .out_31(out_14), .out_32(out_13), .in_18(in_4), .in_19(in_3),
    .in_20(in_2), .in_21(in_1), .out_33(out_12), .out_34(out_11), .out_35(out_10), .out_36(out_9),
    .out_37(out_8), .out_38(out_7), .out_39(out_6), .out_40(out_5));
endmodule

module Registersatz (
  input  In,
  input  in_2,
  input  in_3,
  input  in_4,
  input  in_5,
  input  Out,
  input  St1,
  input  St2,
  input  St3,
  output out_10,
  output out_11,
  output out_12,
  output out_13
);

  wire and_1_out, and_2_out, and_3_out, and_4_out, and_5_out, and_6_out, and_7_out, and_8_out,
       undinout_1_out_4, undinout_1_out_5, undinout_2_out_4, undinout_2_out_5, undinout_3_out_4,
       undinout_3_out_5, undinout_4_out_4, undinout_4_out_5, undinout_5_out_4, undinout_5_out_5,
       undinout_6_out_4, undinout_6_out_5, undinout_7_out_4, undinout_7_out_5, undinout_8_out_4,
       undinout_8_out_5;

  and and_1 (and_1_out, St1, St2, St3);
  and and_2 (and_2_out, St1, St2, ~St3);  // AND_Gate
  and and_3 (and_3_out, St1, ~St2, St3);  // AND_Gate
  and and_4 (and_4_out, St1, ~St2, ~St3);  // AND_Gate
  and and_5 (and_5_out, ~St1, St2, St3);  // AND_Gate
  and and_6 (and_6_out, ~St1, St2, ~St3);  // AND_Gate
  and and_7 (and_7_out, ~St1, ~St2, St3);  // AND_Gate
  and and_8 (and_8_out, ~St1, ~St2, ~St3);  // AND_Gate
  undInOut undinout_1 (.in_2(In), .in_3(Out), .in_1(and_1_out), .out_4(undinout_1_out_4), .out_5(undinout_1_out_5));
  Register AX (
    .RegIn(undinout_1_out_4), .RegOut(undinout_1_out_5), .MSB(in_2), .in_2(in_3), .in_3(in_4), .LSB(in_5),
    .out_7(out_10), .out_8(out_11), .out_9(out_12), .out_10(out_13));
  Register BX (
    .RegIn(undinout_2_out_4), .RegOut(undinout_2_out_5), .MSB(in_2), .in_2(in_3), .in_3(in_4), .LSB(in_5),
    .out_7(out_10), .out_8(out_11), .out_9(out_12), .out_10(out_13));
  undInOut undinout_2 (.in_2(In), .in_3(Out), .in_1(and_2_out), .out_4(undinout_2_out_4), .out_5(undinout_2_out_5));
  Register CX (
    .RegIn(undinout_3_out_4), .RegOut(undinout_3_out_5), .MSB(in_2), .in_2(in_3), .in_3(in_4), .LSB(in_5),
    .out_7(out_10), .out_8(out_11), .out_9(out_12), .out_10(out_13));
  undInOut undinout_3 (.in_2(In), .in_3(Out), .in_1(and_3_out), .out_4(undinout_3_out_4), .out_5(undinout_3_out_5));
  Register DX (
    .RegIn(undinout_4_out_4), .RegOut(undinout_4_out_5), .MSB(in_2), .in_2(in_3), .in_3(in_4), .LSB(in_5),
    .out_7(out_10), .out_8(out_11), .out_9(out_12), .out_10(out_13));
  undInOut undinout_4 (.in_2(In), .in_3(Out), .in_1(and_4_out), .out_4(undinout_4_out_4), .out_5(undinout_4_out_5));
  undInOut undinout_5 (.in_2(In), .in_3(Out), .in_1(and_5_out), .out_4(undinout_5_out_4), .out_5(undinout_5_out_5));
  Register EX (
    .RegIn(undinout_5_out_4), .RegOut(undinout_5_out_5), .MSB(in_2), .in_2(in_3), .in_3(in_4), .LSB(in_5),
    .out_7(out_10), .out_8(out_11), .out_9(out_12), .out_10(out_13));
  Register FX (
    .RegIn(undinout_6_out_4), .RegOut(undinout_6_out_5), .MSB(in_2), .in_2(in_3), .in_3(in_4), .LSB(in_5),
    .out_7(out_10), .out_8(out_11), .out_9(out_12), .out_10(out_13));
  undInOut undinout_6 (.in_2(In), .in_3(Out), .in_1(and_6_out), .out_4(undinout_6_out_4), .out_5(undinout_6_out_5));
  Register GX (
    .RegIn(undinout_7_out_4), .RegOut(undinout_7_out_5), .MSB(in_2), .in_2(in_3), .in_3(in_4), .LSB(in_5),
    .out_7(out_10), .out_8(out_11), .out_9(out_12), .out_10(out_13));
  undInOut undinout_7 (.in_2(In), .in_3(Out), .in_1(and_7_out), .out_4(undinout_7_out_4), .out_5(undinout_7_out_5));
  Register HX (
    .RegIn(undinout_8_out_4), .RegOut(undinout_8_out_5), .MSB(in_2), .in_2(in_3), .in_3(in_4), .LSB(in_5),
    .out_7(out_10), .out_8(out_11), .out_9(out_12), .out_10(out_13));
  undInOut undinout_8 (.in_2(In), .in_3(Out), .in_1(and_8_out), .out_4(undinout_8_out_4), .out_5(undinout_8_out_5));
endmodule

// Reg
module Register (
  input  MSB,
  input  in_2,
  input  in_3,
  input  LSB,
  input  RegIn,
  input  RegOut,
  output out_7,
  output out_8,
  output out_9,
  output out_10
);

  wire d_ff_1_q, d_ff_2_q, d_ff_3_q, d_ff_4_q;

  D_Flip_Flop d_ff_1 (.clk(RegIn), .D(MSB), .Q(d_ff_1_q));  // open: Qn, preset, en, reset
  assign out_7 = RegOut ? d_ff_1_q : 1'bz;  // Controlled_Buffer controlled_buffer_1
  D_Flip_Flop d_ff_2 (.clk(RegIn), .D(in_2), .Q(d_ff_2_q));  // open: Qn, preset, en, reset
  assign out_8 = RegOut ? d_ff_2_q : 1'bz;  // Controlled_Buffer controlled_buffer_2
  D_Flip_Flop d_ff_3 (.clk(RegIn), .D(in_3), .Q(d_ff_3_q));  // open: Qn, preset, en, reset
  assign out_9 = RegOut ? d_ff_3_q : 1'bz;  // Controlled_Buffer controlled_buffer_3
  D_Flip_Flop d_ff_4 (.clk(RegIn), .D(LSB), .Q(d_ff_4_q));  // open: Qn, preset, en, reset
  assign out_10 = RegOut ? d_ff_4_q : 1'bz;  // Controlled_Buffer controlled_buffer_4
endmodule

// uInOut
module undInOut (
  input  in_1,
  input  in_2,
  input  in_3,
  output out_4,
  output out_5
);

  and and_1 (out_4, in_1, in_2);
  and and_2 (out_5, in_1, in_3);
endmodule

module Addresswerk (
  input  in_1,
  input  in_2,
  input  in_3,
  input  in_4,
  input  CSIn,
  input  CSOut,
  input  IPExtIn,
  input  IPIn,
  input  IPInc,
  input  DSIn,
  input  DSOut,
  input  SIIn,
  input  ESIn,
  input  ESOut,
  input  DIIn,
  input  SSIn,
  input  BPIn,
  input  SSBPOut,
  input  SPExtIn,
  input  SPIn,
  input  SPInc,
  input  SPDec,
  input  SSSPOut,
  output out_24,
  output out_25,
  output out_26,
  output out_27,
  output out_28,
  output out_29,
  output out_30,
  output out_31
);

  wire or_1_out;

  or or_1 (or_1_out, SSBPOut, SSSPOut);
  Register CS (
    .RegIn(CSIn), .RegOut(CSOut), .MSB(in_1), .in_2(in_2), .in_3(in_3), .LSB(in_4), .out_7(out_24),
    .out_8(out_25), .out_9(out_26), .out_10(out_27));
  Register ES (
    .RegIn(ESIn), .RegOut(ESOut), .MSB(in_1), .in_2(in_2), .in_3(in_3), .LSB(in_4), .out_7(out_24),
    .out_8(out_25), .out_9(out_26), .out_10(out_27));
  InstructionPointer instructionpointer_1 (
    .ExtIn(IPExtIn), .In(IPIn), .Out(CSOut), .IncIn(IPInc), .in_1(in_1), .in_2(in_2), .in_3(in_3),
    .in_4(in_4), .out_9(out_28), .out_10(out_29), .out_11(out_30), .out_12(out_31));
  Register DI (
    .RegIn(DIIn), .RegOut(ESOut), .MSB(in_1), .in_2(in_2), .in_3(in_3), .LSB(in_4), .out_7(out_31),
    .out_8(out_30), .out_9(out_29), .out_10(out_28));
  Register DS (
    .RegIn(DSIn), .RegOut(DSOut), .MSB(in_1), .in_2(in_2), .in_3(in_3), .LSB(in_4), .out_7(out_24),
    .out_8(out_25), .out_9(out_26), .out_10(out_27));
  Register SS (
    .RegIn(SSIn), .RegOut(or_1_out), .MSB(in_1), .in_2(in_2), .in_3(in_3), .LSB(in_4), .out_7(out_24),
    .out_8(out_25), .out_9(out_26), .out_10(out_27));
  Register SI (
    .RegIn(SIIn), .RegOut(DSOut), .MSB(in_1), .in_2(in_2), .in_3(in_3), .LSB(in_4), .out_7(out_28),
    .out_8(out_29), .out_9(out_30), .out_10(out_31));
  Register BP (
    .RegIn(BPIn), .RegOut(SSBPOut), .MSB(in_1), .in_2(in_2), .in_3(in_3), .LSB(in_4), .out_7(out_31),
    .out_8(out_30), .out_9(out_29), .out_10(out_28));
  StackPointer stackpointer_1 (
    .ExtIn(SPExtIn), .In(SPIn), .IncIn(SPInc), .DecIn(SPDec), .Out(SSSPOut), .in_1(in_1), .in_2(in_2),
    .in_3(in_3), .in_4(in_4), .out_10(out_28), .out_11(out_29), .out_12(out_30), .out_13(out_31));
endmodule

// IP
module InstructionPointer (
  input  in_1,
  input  in_2,
  input  in_3,
  input  in_4,
  input  ExtIn,
  input  In,
  input  Out,
  input  IncIn,
  output out_9,
  output out_10,
  output out_11,
  output out_12
);

  wire controlled_buffer_1_out, controlled_buffer_2_out, controlled_buffer_3_out, controlled_buffer_6_out,
       d_ff_1_q, d_ff_2_q, d_ff_3_q, d_ff_4_q, halbaddierer_1_out_4, halbaddierer_2_out_3,
       halbaddierer_2_out_4, halbaddierer_3_out_3, halbaddierer_3_out_4, halbaddierer_4_out_3,
       halbaddierer_4_out_4;

  assign controlled_buffer_1_out = ExtIn ? in_1 : 1'bz;  // Controlled_Buffer controlled_buffer_1
  halbAddierer halbaddierer_1 (
    .in_1(d_ff_1_q), .in_2(halbaddierer_2_out_3), .out_4(halbaddierer_1_out_4));  // open: out_3
  assign controlled_buffer_2_out = ExtIn ? in_3 : 1'bz;  // Controlled_Buffer controlled_buffer_2
  assign controlled_buffer_3_out = ExtIn ? in_2 : 1'bz;  // Controlled_Buffer controlled_buffer_3
  D_Flip_Flop d_ff_1 (.clk(In), .D(controlled_buffer_1_out), .Q(d_ff_1_q));  // open: Qn, preset, en, reset
  halbAddierer halbaddierer_2 (
    .in_1(d_ff_2_q), .in_2(halbaddierer_3_out_3), .out_3(halbaddierer_2_out_3), .out_4(halbaddierer_2_out_4));
  assign controlled_buffer_1_out = IncIn ? halbaddierer_1_out_4 : 1'bz;  // Controlled_Buffer controlled_buffer_4
  assign controlled_buffer_3_out = IncIn ? halbaddierer_2_out_4 : 1'bz;  // Controlled_Buffer controlled_buffer_5
  assign controlled_buffer_6_out = ExtIn ? in_4 : 1'bz;  // Controlled_Buffer controlled_buffer_6
  D_Flip_Flop d_ff_2 (.clk(In), .D(controlled_buffer_3_out), .Q(d_ff_2_q));  // open: Qn, preset, en, reset
  halbAddierer halbaddierer_3 (
    .in_1(d_ff_3_q), .in_2(halbaddierer_4_out_3), .out_3(halbaddierer_3_out_3), .out_4(halbaddierer_3_out_4));
  halbAddierer halbaddierer_4 (
    .in_1(d_ff_4_q), .in_2(1'b1), .out_3(halbaddierer_4_out_3), .out_4(halbaddierer_4_out_4));
  assign controlled_buffer_2_out = IncIn ? halbaddierer_3_out_4 : 1'bz;  // Controlled_Buffer controlled_buffer_7
  assign controlled_buffer_6_out = IncIn ? halbaddierer_4_out_4 : 1'bz;  // Controlled_Buffer controlled_buffer_8
  D_Flip_Flop d_ff_3 (.clk(In), .D(controlled_buffer_2_out), .Q(d_ff_3_q));  // open: Qn, preset, en, reset
  assign out_9 = Out ? d_ff_1_q : 1'bz;  // Controlled_Buffer controlled_buffer_9
  assign out_10 = Out ? d_ff_2_q : 1'bz;  // Controlled_Buffer controlled_buffer_10
  D_Flip_Flop d_ff_4 (.clk(In), .D(controlled_buffer_6_out), .Q(d_ff_4_q));  // open: Qn, preset, en, reset
  assign out_11 = Out ? d_ff_3_q : 1'bz;  // Controlled_Buffer controlled_buffer_11
  assign out_12 = Out ? d_ff_4_q : 1'bz;  // Controlled_Buffer controlled_buffer_12
endmodule

// HA
module halbAddierer (
  input  in_1,
  input  in_2,
  output out_3,
  output out_4
);

  and and_1 (out_3, in_1, in_2);
  xor xor_1 (out_4, in_1, in_2);
endmodule

// SP
module StackPointer (
  input  in_1,
  input  in_2,
  input  in_3,
  input  in_4,
  input  ExtIn,
  input  In,
  input  IncIn,
  input  DecIn,
  input  Out,
  output out_10,
  output out_11,
  output out_12,
  output out_13
);

  wire controlled_buffer_1_out, controlled_buffer_2_out, controlled_buffer_3_out, controlled_buffer_6_out,
       d_ff_1_q, d_ff_2_q, d_ff_3_q, d_ff_4_q, halbaddierer_1_out_4, halbaddierer_2_out_3,
       halbaddierer_2_out_4, halbaddierer_3_out_3, halbaddierer_3_out_4, halbaddierer_4_out_3,
       halbaddierer_4_out_4, halbaddierer_5_out_3, halbaddierer_5_out_4, volladdierer_1_out_4,
       volladdierer_2_out_4, volladdierer_2_out_5, volladdierer_3_out_4, volladdierer_3_out_5;

  assign controlled_buffer_1_out = ExtIn ? in_1 : 1'bz;  // Controlled_Buffer controlled_buffer_1
  halbAddierer halbaddierer_1 (
    .in_1(d_ff_1_q), .in_2(halbaddierer_2_out_3), .out_4(halbaddierer_1_out_4));  // open: out_3
  assign controlled_buffer_2_out = ExtIn ? in_3 : 1'bz;  // Controlled_Buffer controlled_buffer_2
  assign controlled_buffer_3_out = ExtIn ? in_2 : 1'bz;  // Controlled_Buffer controlled_buffer_3
  D_Flip_Flop d_ff_1 (.clk(In), .D(controlled_buffer_1_out), .Q(d_ff_1_q));  // open: Qn, preset, en, reset
  halbAddierer halbaddierer_2 (
    .in_1(d_ff_2_q), .in_2(halbaddierer_3_out_3), .out_3(halbaddierer_2_out_3), .out_4(halbaddierer_2_out_4));
  assign controlled_buffer_1_out = IncIn ? halbaddierer_1_out_4 : 1'bz;  // Controlled_Buffer controlled_buffer_4
  assign controlled_buffer_3_out = IncIn ? halbaddierer_2_out_4 : 1'bz;  // Controlled_Buffer controlled_buffer_5
  assign controlled_buffer_6_out = ExtIn ? in_4 : 1'bz;  // Controlled_Buffer controlled_buffer_6
  D_Flip_Flop d_ff_2 (.clk(In), .D(controlled_buffer_3_out), .Q(d_ff_2_q));  // open: Qn, preset, en, reset
  halbAddierer halbaddierer_3 (
    .in_1(d_ff_3_q), .in_2(halbaddierer_4_out_3), .out_3(halbaddierer_3_out_3), .out_4(halbaddierer_3_out_4));
  halbAddierer halbaddierer_4 (
    .in_1(d_ff_4_q), .in_2(1'b1), .out_3(halbaddierer_4_out_3), .out_4(halbaddierer_4_out_4));
  assign controlled_buffer_6_out = IncIn ? halbaddierer_4_out_4 : 1'bz;  // Controlled_Buffer controlled_buffer_7
  assign controlled_buffer_2_out = IncIn ? halbaddierer_3_out_4 : 1'bz;  // Controlled_Buffer controlled_buffer_8
  D_Flip_Flop d_ff_3 (.clk(In), .D(controlled_buffer_2_out), .Q(d_ff_3_q));  // open: Qn, preset, en, reset
  vollAddierer volladdierer_1 (
    .in_1(d_ff_1_q), .in_2(1'b1), .in_3(volladdierer_3_out_5), .out_4(volladdierer_1_out_4));  // open: out_5
  assign controlled_buffer_1_out = DecIn ? volladdierer_1_out_4 : 1'bz;  // Controlled_Buffer controlled_buffer_9
  D_Flip_Flop d_ff_4 (.clk(In), .D(controlled_buffer_6_out), .Q(d_ff_4_q));  // open: Qn, preset, en, reset
  vollAddierer volladdierer_2 (
    .in_1(d_ff_3_q), .in_2(1'b1), .in_3(halbaddierer_5_out_3), .out_5(volladdierer_2_out_5),
    .out_4(volladdierer_2_out_4));
  vollAddierer volladdierer_3 (
    .in_1(d_ff_2_q), .in_2(1'b1), .in_3(volladdierer_2_out_5), .out_5(volladdierer_3_out_5),
    .out_4(volladdierer_3_out_4));
  assign controlled_buffer_3_out = DecIn ? volladdierer_3_out_4 : 1'bz;  // Controlled_Buffer controlled_buffer_10
  assign controlled_buffer_2_out = DecIn ? volladdierer_2_out_4 : 1'bz;  // Controlled_Buffer controlled_buffer_11
  halbAddierer halbaddierer_5 (
    .in_1(d_ff_4_q), .in_2(1'b1), .out_3(halbaddierer_5_out_3), .out_4(halbaddierer_5_out_4));
  assign controlled_buffer_6_out = DecIn ? halbaddierer_5_out_4 : 1'bz;  // Controlled_Buffer controlled_buffer_12
  assign out_10 = Out ? d_ff_1_q : 1'bz;  // Controlled_Buffer controlled_buffer_13
  assign out_11 = Out ? d_ff_2_q : 1'bz;  // Controlled_Buffer controlled_buffer_14
  assign out_13 = Out ? d_ff_4_q : 1'bz;  // Controlled_Buffer controlled_buffer_15
  assign out_12 = Out ? d_ff_3_q : 1'bz;  // Controlled_Buffer controlled_buffer_16
endmodule

module BIU (
  input  in_1,
  input  in_2,
  input  in_3,
  input  in_4,
  input  in_5,
  input  in_6,
  input  in_7,
  input  in_8,
  input  in_9,
  input  in_10,
  input  in_11,
  input  in_12,
  input  In,
  input  G,
  input  Dir,
  input  Out1,
  input  Out2,
  input  in_18,
  input  in_19,
  input  in_20,
  input  in_21,
  input  In_13,
  input  G_2,
  input  Out1_2,
  output out_25,
  output out_26,
  output out_27,
  output out_28,
  output out_29,
  output out_30,
  output out_31,
  output out_32,
  output out_33,
  output out_34,
  output out_35,
  output out_36,
  output out_37,
  output out_38,
  output out_39,
  output out_40
);

  Datenbustreiber datenbustreiber_1 (
    .In(In), .G(G), .Dir(Dir), .Out1(Out1), .Out2(Out2), .out_14(out_25), .out_15(out_26), .out_16(out_27),
    .out_17(out_28), .in_1(in_1), .in_2(in_2), .in_3(in_3), .in_4(in_4), .out_18(out_29), .out_19(out_30),
    .out_20(out_31), .out_21(out_32), .in_10(in_18), .in_11(in_19), .in_12(in_20), .in_13(in_21));
  Addressbustreiber addressbustreiber_1 (
    .In(In_13), .G(G_2), .Out1(Out1_2), .in_1(in_5), .in_2(in_6), .in_3(in_7), .in_4(in_8), .in_5(in_9),
    .in_6(in_10), .in_7(in_11), .in_8(in_12), .out_12(out_33), .out_13(out_34), .out_14(out_35),
    .out_15(out_36), .out_16(out_37), .out_17(out_38), .out_18(out_39), .out_19(out_40));
endmodule

module Datenbustreiber (
  input  in_1,
  input  in_2,
  input  in_3,
  input  in_4,
  input  In,
  input  G,
  input  Dir,
  input  Out1,
  input  Out2,
  input  in_10,
  input  in_11,
  input  in_12,
  input  in_13,
  output out_14,
  output out_15,
  output out_16,
  output out_17,
  output out_18,
  output out_19,
  output out_20,
  output out_21
);

  BidirektionalesSpeicherding bidirektionalesspeicherding_1 (
    .In(In), .G(G), .Dir(Dir), .Out1(Out1), .Out2(Out2), .out_8(out_14), .in_2(in_1), .out_9(out_18),
    .in_7(in_10));
  BidirektionalesSpeicherding bidirektionalesspeicherding_2 (
    .In(In), .G(G), .Dir(Dir), .Out1(Out1), .Out2(Out2), .out_8(out_15), .in_2(in_2), .out_9(out_19),
    .in_7(in_11));
  BidirektionalesSpeicherding bidirektionalesspeicherding_3 (
    .In(In), .G(G), .Dir(Dir), .Out1(Out1), .Out2(Out2), .out_8(out_16), .in_2(in_3), .out_9(out_20),
    .in_7(in_12));
  BidirektionalesSpeicherding bidirektionalesspeicherding_4 (
    .In(In), .G(G), .Dir(Dir), .Out1(Out1), .Out2(Out2), .out_8(out_17), .in_2(in_4), .out_9(out_21),
    .in_7(in_13));
endmodule

// DI
module BidirektionalesSpeicherding (
  input  In,
  input  in_2,
  input  G,
  input  Dir,
  input  Out1,
  input  Out2,
  input  in_7,
  output out_8,
  output out_9
);

  wire and_1_out, and_2_out, and_3_out, and_4_out, controlled_buffer_2_out, d_ff_1_q;

  and and_1 (and_1_out, G, Dir);
  and and_2 (and_2_out, G, ~Dir);  // AND_Gate
  assign out_8 = and_3_out ? d_ff_1_q : 1'bz;  // Controlled_Buffer controlled_buffer_1
  and and_3 (and_3_out, Out1, and_1_out);
  assign controlled_buffer_2_out = and_1_out ? in_2 : 1'bz;  // Controlled_Buffer controlled_buffer_2
  D_Flip_Flop d_ff_1 (.clk(In), .D(controlled_buffer_2_out), .Q(d_ff_1_q));  // open: Qn, preset, en, reset
  assign controlled_buffer_2_out = and_2_out ? in_7 : 1'bz;  // Controlled_Buffer controlled_buffer_3
  and and_4 (and_4_out, and_2_out, Out2);
  assign out_9 = and_4_out ? d_ff_1_q : 1'bz;  // Controlled_Buffer controlled_buffer_4
endmodule

module Addressbustreiber (
  input  in_1,
  input  in_2,
  input  in_3,
  input  in_4,
  input  in_5,
  input  in_6,
  input  in_7,
  input  in_8,
  input  In,
  input  G,
  input  Out1,
  output out_12,
  output out_13,
  output out_14,
  output out_15,
  output out_16,
  output out_17,
  output out_18,
  output out_19
);

  UnidirektionalesSpeicherDing unidirektionalesspeicherding_1 (
    .In(In), .G(G), .Out1(Out1), .in_2(in_1), .out_5(out_12));
  UnidirektionalesSpeicherDing unidirektionalesspeicherding_2 (
    .In(In), .G(G), .Out1(Out1), .in_2(in_2), .out_5(out_13));
  UnidirektionalesSpeicherDing unidirektionalesspeicherding_3 (
    .In(In), .G(G), .Out1(Out1), .in_2(in_3), .out_5(out_14));
  UnidirektionalesSpeicherDing unidirektionalesspeicherding_4 (
    .In(In), .G(G), .Out1(Out1), .in_2(in_4), .out_5(out_15));
  UnidirektionalesSpeicherDing unidirektionalesspeicherding_5 (
    .In(In), .G(G), .Out1(Out1), .in_2(in_5), .out_5(out_16));
  UnidirektionalesSpeicherDing unidirektionalesspeicherding_6 (.In(In), .in_2(in_6), .out_5(out_17));  // open: G, Out1
  UnidirektionalesSpeicherDing unidirektionalesspeicherding_7 (
    .In(In), .G(G), .Out1(Out1), .in_2(in_7), .out_5(out_18));
  UnidirektionalesSpeicherDing unidirektionalesspeicherding_8 (
    .In(In), .G(G), .Out1(Out1), .in_2(in_8), .out_5(out_19));
endmodule

// AI
module UnidirektionalesSpeicherDing (
  input  In,
  input  in_2,
  input  G,
  input  Out1,
  output out_5
);

  wire and_1_out, controlled_buffer_1_out, d_ff_1_q;

  assign controlled_buffer_1_out = G ? in_2 : 1'bz;  // Controlled_Buffer controlled_buffer_1
  D_Flip_Flop d_ff_1 (.clk(In), .D(controlled_buffer_1_out), .Q(d_ff_1_q));  // open: Qn, preset, en, reset
  and and_1 (and_1_out, Out1, G);
  assign out_5 = and_1_out ? d_ff_1_q : 1'bz;  // Controlled_Buffer controlled_buffer_2
endmodule

module Steuerwerk (
  input  in_1,
  input  in_2,
  input  in_3,
  input  in_4,
  input  Takt,
  output BIU,
  output out_7,
  output out_8,
  output out_9,
  output out_10,
  output out_11,
  output out_12,
  output out_13,
  output Registersatz,
  output out_15,
  output out_16,
  output out_17,
  output out_18,
  output Addresswerk,
  output out_20,
  output out_21,
  output out_22,
  output out_23,
  output out_24,
  output out_25,
  output out_26,
  output out_27,
  output out_28,
  output out_29,
  output out_30,
  output out_31,
  output out_32,
  output out_33,
  output out_34,
  output out_35,
  output out_36,
  output out_37,
  output ALU,
  output out_39,
  output out_40,
  output out_41,
  output out_42,
  output out_43,
  output out_44,
  output out_45,
  output out_46,
  output out_47,
  output out_48,
  output out_49,
  output out_50,
  output out_51
);

  wire befehlsregister_1_out_7, befehlsregister_1_out_8, befehlsregister_1_out_9, befehlsregister_1_out_10,
       decoder_1_out_6, decoder_1_out_7, decoder_1_out_8, decoder_1_out_9, decoder_1_out_10,
       decoder_1_out_11, decoder_1_out_12, decoder_1_out_13, steuerwort_1_out_51, steuerwort_1_out_52,
       steuerwort_1_out_53;

  Befehlsregister befehlsregister_1 (
    .In(steuerwort_1_out_51), .Next(steuerwort_1_out_52), .in_1(in_1), .in_2(in_2), .in_3(in_3), .in_4(in_4),
    .out_7(befehlsregister_1_out_7), .out_8(befehlsregister_1_out_8), .out_9(befehlsregister_1_out_9),
    .out_10(befehlsregister_1_out_10));
  Decoder decoder_1 (
    .Out(steuerwort_1_out_53), .in_1(befehlsregister_1_out_7), .in_2(befehlsregister_1_out_8),
    .in_3(befehlsregister_1_out_9), .in_4(befehlsregister_1_out_10), .out_6(decoder_1_out_6),
    .out_7(decoder_1_out_7), .out_8(decoder_1_out_8), .out_9(decoder_1_out_9), .out_10(decoder_1_out_10),
    .out_11(decoder_1_out_11), .out_12(decoder_1_out_12), .out_13(decoder_1_out_13));
  AddressDecoder addressdecoder_1 (
    .in_1(decoder_1_out_6), .in_2(decoder_1_out_7), .in_3(decoder_1_out_8), .in_4(decoder_1_out_9),
    .in_5(decoder_1_out_10), .in_6(decoder_1_out_11), .in_7(decoder_1_out_12), .in_8(decoder_1_out_13));  // open: out_9, out_10, out_11, out_12, out_13, out_14, out_15, out_16
  FolgeAddresse folgeaddresse_1 (
    .Takt(Takt), .Out(steuerwort_1_out_53), .out_11(decoder_1_out_6), .out_12(decoder_1_out_7),
    .out_13(decoder_1_out_8), .out_14(decoder_1_out_9), .out_15(decoder_1_out_10), .out_16(decoder_1_out_11),
    .out_17(decoder_1_out_12), .out_18(decoder_1_out_13));  // open: in_1, in_2, in_3, in_4, in_5, in_6, in_7, in_8
  Steuerwort steuerwort_1 (
    .Takt(Takt), .out_51(steuerwort_1_out_51), .out_52(steuerwort_1_out_52), .out_53(steuerwort_1_out_53),
    .out_54(BIU), .out_55(out_7), .out_56(out_8), .out_57(out_9), .out_58(out_10), .out_59(out_11),
    .out_60(out_12), .out_61(out_13), .out_62(Registersatz), .out_63(out_15), .out_64(out_16),
    .out_65(out_17), .out_66(out_18), .out_67(Addresswerk), .out_68(out_20), .out_69(out_21),
    .out_70(out_22), .out_71(out_23), .out_72(out_24), .out_73(out_25), .out_74(out_26), .out_75(out_27),
    .out_76(out_28), .out_77(out_29), .out_78(out_30), .out_79(out_31), .out_80(out_32), .out_81(out_33),
    .out_82(out_34), .out_83(out_35), .out_84(out_36), .out_85(out_37), .out_86(ALU), .out_87(out_39),
    .out_88(out_40), .out_89(out_41), .out_90(out_42), .out_91(out_43), .out_92(out_44), .out_93(out_45),
    .out_94(out_46), .out_95(out_47), .out_96(out_48), .out_97(out_49), .out_98(out_50), .out_99(out_51));  // open: Befehlsregister, in_2, Decoder, BIU, in_5, in_6, in_7, in_8, in_9, in_10, in_11, Registersatz, in_13, in_14, in_15, in_16, Addresswerk, in_18, in_19, in_20, in_21, in_22, in_23, in_24, in_25, in_26, in_27, in_28, in_29, in_30, in_31, in_32, in_33, in_34, in_35, ALU, in_37, in_38, in_39, in_40, in_41, in_42, in_43, in_44, in_45, in_46, in_47, in_48, in_49
endmodule

module Befehlsregister (
  input  in_1,
  input  in_2,
  input  in_3,
  input  in_4,
  input  In,
  input  Next,
  output out_7,
  output out_8,
  output out_9,
  output out_10
);

  wire register_2_out_7, register_2_out_8, register_2_out_9, register_2_out_10, register_3_out_7,
       register_3_out_8, register_3_out_9, register_3_out_10;

  Register register_1 (
    .RegIn(Next), .RegOut(1'b1), .MSB(register_2_out_7), .in_2(register_2_out_8), .in_3(register_2_out_9),
    .LSB(register_2_out_10), .out_7(out_7), .out_8(out_8), .out_9(out_9), .out_10(out_10));
  Register register_2 (
    .RegIn(Next), .RegOut(1'b1), .MSB(register_3_out_7), .in_2(register_3_out_8), .in_3(register_3_out_9),
    .LSB(register_3_out_10), .out_7(register_2_out_7), .out_8(register_2_out_8), .out_9(register_2_out_9),
    .out_10(register_2_out_10));
  Register register_3 (
    .RegIn(In), .RegOut(1'b1), .MSB(in_1), .in_2(in_2), .in_3(in_3), .LSB(in_4), .out_7(register_3_out_7),
    .out_8(register_3_out_8), .out_9(register_3_out_9), .out_10(register_3_out_10));
endmodule

module Decoder (
  input  in_1,
  input  in_2,
  input  in_3,
  input  in_4,
  input  Out,
  output out_6,
  output out_7,
  output out_8,
  output out_9,
  output out_10,
  output out_11,
  output out_12,
  output out_13
);

  wire not_1_out, undriven, undriven_2, undriven_3, undriven_4;

  Dec dec_1 (
    .Out(Out), .in_1(in_1), .in_2(in_2), .in_3(in_3), .in_4(in_4), .in_5(undriven), .in_6(undriven_2),
    .in_7(undriven_3), .in_8(undriven_4), .out_10(out_6), .out_11(out_7), .out_12(out_8), .out_13(out_9),
    .out_14(out_10), .out_15(out_11), .out_16(out_12), .out_17(out_13));
  Dec dec_2 (
    .Out(Out), .in_1(in_1), .in_2(in_2), .in_3(in_3), .in_4(in_4), .in_5(undriven), .in_6(undriven_2),
    .in_7(undriven_3), .in_8(not_1_out), .out_10(out_6), .out_11(out_7), .out_12(out_8), .out_13(out_9),
    .out_14(out_10), .out_15(out_11), .out_16(out_12), .out_17(out_13));
  not not_1 (not_1_out, undriven_4);
  Dec dec_3 (.Out(Out));  // open: in_1, in_2, in_3, in_4, in_5, in_6, in_7, in_8, out_10, out_11, out_12, out_13, out_14, out_15, out_16, out_17
  Dec dec_4 (.Out(Out));  // open: in_1, in_2, in_3, in_4, in_5, in_6, in_7, in_8, out_10, out_11, out_12, out_13, out_14, out_15, out_16, out_17
  Dec dec_5 (.Out(Out));  // open: in_1, in_2, in_3, in_4, in_5, in_6, in_7, in_8, out_10, out_11, out_12, out_13, out_14, out_15, out_16, out_17
  Dec dec_6 (.Out(Out));  // open: in_1, in_2, in_3, in_4, in_5, in_6, in_7, in_8, out_10, out_11, out_12, out_13, out_14, out_15, out_16, out_17
  Dec dec_7 (.Out(Out));  // open: in_1, in_2, in_3, in_4, in_5, in_6, in_7, in_8, out_10, out_11, out_12, out_13, out_14, out_15, out_16, out_17
  Dec dec_8 (
    .Out(Out), .in_1(in_1), .in_2(in_2), .in_3(in_3), .in_4(in_4), .in_5(undriven), .in_6(undriven_2),
    .in_7(undriven_3), .in_8(undriven_4), .out_10(out_6), .out_11(out_7), .out_12(out_8), .out_13(out_9),
    .out_14(out_10), .out_15(out_11), .out_16(out_12), .out_17(out_13));
endmodule

module AddressDecoder (
  input  in_1,
  input  in_2,
  input  in_3,
  input  in_4,
  input  in_5,
  input  in_6,
  input  in_7,
  input  in_8,
  output out_9,
  output out_10,
  output out_11,
  output out_12,
  output out_13,
  output out_14,
  output out_15,
  output out_16
);

  and and_1 (out_9, in_1, in_2, in_3, in_4, in_5, in_6, in_7, in_8);
  and and_2 (out_10, in_1, in_2, in_3, in_4, in_5, in_6, in_7, ~in_8);  // AND_Gate
  and and_3 (out_11, in_1, in_2, in_3, in_4, in_5, in_6, ~in_7, in_8);  // AND_Gate
  and and_4 (out_12, in_1, in_2, in_3, in_4, in_5, in_6, ~in_7, in_8);  // AND_Gate
endmodule

module Dec (
  input  in_1,
  input  in_2,
  input  in_3,
  input  in_4,
  input  in_5,
  input  in_6,
  input  in_7,
  input  in_8,
  input  Out,
  output out_10,
  output out_11,
  output out_12,
  output out_13,
  output out_14,
  output out_15,
  output out_16,
  output out_17
);

  wire and_1_out, and_2_out, not_1_out;

  and and_1 (and_1_out, ~in_1, ~in_2, ~in_3, ~in_4, ~in_5, ~in_6, ~in_7, ~in_8);  // AND_Gate
  not not_1 (not_1_out, and_1_out);
  and and_2 (and_2_out, ~not_1_out, Out);  // AND_Gate
  assign out_10 = and_2_out ? not_1_out : 1'bz;  // Controlled_Buffer controlled_buffer_1

  assign out_11 = out_10;
  assign out_12 = out_10;
  assign out_13 = out_10;
  assign out_14 = out_10;
  assign out_15 = out_10;
  assign out_16 = out_10;
  assign out_17 = out_10;
endmodule

module Steuerwort (
  input  Befehlsregister,
  input  in_2,
  input  Decoder,
  input  BIU,
  input  in_5,
  input  in_6,
  input  in_7,
  input  in_8,
  input  in_9,
  input  in_10,
  input  in_11,
  input  Registersatz,
  input  in_13,
  input  in_14,
  input  in_15,
  input  in_16,
  input  Addresswerk,
  input  in_18,
  input  in_19,
  input  in_20,
  input  in_21,
  input  in_22,
  input  in_23,
  input  in_24,
  input  in_25,
  input  in_26,
  input  in_27,
  input  in_28,
  input  in_29,
  input  in_30,
  input  in_31,
  input  in_32,
  input  in_33,
  input  in_34,
  input  in_35,
  input  ALU,
  input  in_37,
  input  in_38,
  input  in_39,
  input  in_40,
  input  in_41,
  input  in_42,
  input  in_43,
  input  in_44,
  input  in_45,
  input  in_46,
  input  in_47,
  input  in_48,
  input  in_49,
  input  Takt,
  output out_51,
  output out_52,
  output out_53,
  output out_54,
  output out_55,
  output out_56,
  output out_57,
  output out_58,
  output out_59,
  output out_60,
  output out_61,
  output out_62,
  output out_63,
  output out_64,
  output out_65,
  output out_66,
  output out_67,
  output out_68,
  output out_69,
  output out_70,
  output out_71,
  output out_72,
  output out_73,
  output out_74,
  output out_75,
  output out_76,
  output out_77,
  output out_78,
  output out_79,
  output out_80,
  output out_81,
  output out_82,
  output out_83,
  output out_84,
  output out_85,
  output out_86,
  output out_87,
  output out_88,
  output out_89,
  output out_90,
  output out_91,
  output out_92,
  output out_93,
  output out_94,
  output out_95,
  output out_96,
  output out_97,
  output out_98,
  output out_99
);

  Steuerspeicher steuerspeicher_1 (.in_2(Takt), .in_1(Befehlsregister), .out_3(out_51));
  Steuerspeicher steuerspeicher_2 (.in_2(Takt), .in_1(in_2), .out_3(out_52));
  Steuerspeicher steuerspeicher_3 (.in_2(Takt), .in_1(Decoder), .out_3(out_53));
  Steuerspeicher steuerspeicher_4 (.in_2(Takt), .in_1(in_5), .out_3(out_55));
  Steuerspeicher steuerspeicher_5 (.in_2(Takt), .in_1(BIU), .out_3(out_54));
  Steuerspeicher steuerspeicher_6 (.in_2(Takt), .in_1(in_6), .out_3(out_56));
  Steuerspeicher steuerspeicher_7 (.in_2(Takt), .in_1(in_8), .out_3(out_58));
  Steuerspeicher steuerspeicher_8 (.in_2(Takt), .in_1(in_7), .out_3(out_57));
  Steuerspeicher steuerspeicher_9 (.in_2(Takt), .in_1(in_9), .out_3(out_59));
  Steuerspeicher steuerspeicher_10 (.in_2(Takt), .in_1(in_10), .out_3(out_60));
  Steuerspeicher steuerspeicher_11 (.in_2(Takt), .in_1(in_11), .out_3(out_61));
  Steuerspeicher steuerspeicher_12 (.in_2(Takt), .in_1(Registersatz), .out_3(out_62));
  Steuerspeicher steuerspeicher_13 (.in_2(Takt), .in_1(in_14), .out_3(out_64));
  Steuerspeicher steuerspeicher_14 (.in_2(Takt), .in_1(in_13), .out_3(out_63));
  Steuerspeicher steuerspeicher_15 (.in_2(Takt), .in_1(in_16), .out_3(out_66));
  Steuerspeicher steuerspeicher_16 (.in_2(Takt), .in_1(in_15), .out_3(out_65));
  Steuerspeicher steuerspeicher_17 (.in_2(Takt), .in_1(Addresswerk), .out_3(out_67));
  Steuerspeicher steuerspeicher_18 (.in_2(Takt), .in_1(in_18), .out_3(out_68));
  Steuerspeicher steuerspeicher_19 (.in_2(Takt), .in_1(in_20), .out_3(out_70));
  Steuerspeicher steuerspeicher_20 (.in_2(Takt), .in_1(in_19), .out_3(out_69));
  Steuerspeicher steuerspeicher_21 (.in_2(Takt), .in_1(in_22), .out_3(out_72));
  Steuerspeicher steuerspeicher_22 (.in_2(Takt), .in_1(in_21), .out_3(out_71));
  Steuerspeicher steuerspeicher_23 (.in_2(Takt), .in_1(in_23), .out_3(out_73));
  Steuerspeicher steuerspeicher_24 (.in_2(Takt), .in_1(in_24), .out_3(out_74));
  Steuerspeicher steuerspeicher_25 (.in_2(Takt), .in_1(in_25), .out_3(out_75));
  Steuerspeicher steuerspeicher_26 (.in_2(Takt), .in_1(in_26), .out_3(out_76));
  Steuerspeicher steuerspeicher_27 (.in_2(Takt), .in_1(in_28), .out_3(out_78));
  Steuerspeicher steuerspeicher_28 (.in_2(Takt), .in_1(in_27), .out_3(out_77));
  Steuerspeicher steuerspeicher_29 (.in_2(Takt), .in_1(in_30), .out_3(out_80));
  Steuerspeicher steuerspeicher_30 (.in_2(Takt), .in_1(in_29), .out_3(out_79));
  Steuerspeicher steuerspeicher_31 (.in_2(Takt), .in_1(in_31), .out_3(out_81));
  Steuerspeicher steuerspeicher_32 (.in_2(Takt), .in_1(in_32), .out_3(out_82));
  Steuerspeicher steuerspeicher_33 (.in_2(Takt), .in_1(in_33), .out_3(out_83));
  Steuerspeicher steuerspeicher_34 (.in_2(Takt), .in_1(in_34), .out_3(out_84));
  Steuerspeicher steuerspeicher_35 (.in_2(Takt), .in_1(ALU), .out_3(out_86));
  Steuerspeicher steuerspeicher_36 (.in_2(Takt), .in_1(in_35), .out_3(out_85));
  Steuerspeicher steuerspeicher_37 (.in_2(Takt), .in_1(in_37), .out_3(out_87));
  Steuerspeicher steuerspeicher_38 (.in_2(Takt), .in_1(in_38), .out_3(out_88));
  Steuerspeicher steuerspeicher_39 (.in_2(Takt), .in_1(in_39), .out_3(out_89));
  Steuerspeicher steuerspeicher_40 (.in_2(Takt), .in_1(in_40), .out_3(out_90));
  Steuerspeicher steuerspeicher_41 (.in_2(Takt), .in_1(in_41), .out_3(out_91));
  Steuerspeicher steuerspeicher_42 (.in_2(Takt), .in_1(in_42), .out_3(out_92));
  Steuerspeicher steuerspeicher_43 (.in_2(Takt), .in_1(in_43), .out_3(out_93));
  Steuerspeicher steuerspeicher_44 (.in_2(Takt), .in_1(in_44), .out_3(out_94));
  Steuerspeicher steuerspeicher_45 (.in_2(Takt), .in_1(in_45), .out_3(out_95));
  Steuerspeicher steuerspeicher_46 (.in_2(Takt), .in_1(in_46), .out_3(out_96));
  Steuerspeicher steuerspeicher_47 (.in_2(Takt), .in_1(in_47), .out_3(out_97));
  Steuerspeicher steuerspeicher_48 (.in_2(Takt), .in_1(in_48), .out_3(out_98));
  Steuerspeicher steuerspeicher_49 (.in_2(Takt), .in_1(in_49), .out_3(out_99));
endmodule

module Steuerspeicher (
  input  in_1,
  input  in_2,
  output out_3
);

  wire d_ff_1_q, not_1_out;

  D_Flip_Flop d_ff_1 (.clk(in_2), .D(in_1), .Q(d_ff_1_q));  // open: Qn, preset, en, reset
  not not_1 (not_1_out, in_2);
  D_Flip_Flop d_ff_2 (.clk(not_1_out), .D(d_ff_1_q), .Q(out_3));  // open: Qn, preset, en, reset
endmodule

// Folgeaddresse
module FolgeAddresse (
  input  in_1,
  input  in_2,
  input  in_3,
  input  in_4,
  input  in_5,
  input  in_6,
  input  in_7,
  input  in_8,
  input  Takt,
  input  Out,
  output out_11,
  output out_12,
  output out_13,
  output out_14,
  output out_15,
  output out_16,
  output out_17,
  output out_18
);

  wire not_1_out, steuerspeicher_1_out_3, steuerspeicher_2_out_3, steuerspeicher_3_out_3,
       steuerspeicher_4_out_3, steuerspeicher_5_out_3, steuerspeicher_6_out_3, steuerspeicher_7_out_3,
       steuerspeicher_8_out_3;

  not not_1 (not_1_out, Out);
  Steuerspeicher steuerspeicher_1 (.in_2(Takt), .in_1(in_1), .out_3(steuerspeicher_1_out_3));
  Steuerspeicher steuerspeicher_2 (.in_2(Takt), .in_1(in_2), .out_3(steuerspeicher_2_out_3));
  assign out_11 = not_1_out ? steuerspeicher_1_out_3 : 1'bz;  // Controlled_Buffer controlled_buffer_1
  assign out_12 = not_1_out ? steuerspeicher_2_out_3 : 1'bz;  // Controlled_Buffer controlled_buffer_2
  Steuerspeicher steuerspeicher_3 (.in_2(Takt), .in_1(in_3), .out_3(steuerspeicher_3_out_3));
  assign out_13 = not_1_out ? steuerspeicher_3_out_3 : 1'bz;  // Controlled_Buffer controlled_buffer_3
  Steuerspeicher steuerspeicher_4 (.in_2(Takt), .in_1(in_4), .out_3(steuerspeicher_4_out_3));
  Steuerspeicher steuerspeicher_5 (.in_2(Takt), .in_1(in_5), .out_3(steuerspeicher_5_out_3));
  assign out_14 = not_1_out ? steuerspeicher_4_out_3 : 1'bz;  // Controlled_Buffer controlled_buffer_4
  assign out_15 = not_1_out ? steuerspeicher_5_out_3 : 1'bz;  // Controlled_Buffer controlled_buffer_5
  Steuerspeicher steuerspeicher_6 (.in_2(Takt), .in_1(in_7), .out_3(steuerspeicher_6_out_3));
  Steuerspeicher steuerspeicher_7 (.in_2(Takt), .in_1(in_6), .out_3(steuerspeicher_7_out_3));
  assign out_16 = not_1_out ? steuerspeicher_7_out_3 : 1'bz;  // Controlled_Buffer controlled_buffer_6
  assign out_17 = not_1_out ? steuerspeicher_6_out_3 : 1'bz;  // Controlled_Buffer controlled_buffer_7
  Steuerspeicher steuerspeicher_8 (.in_2(Takt), .in_1(in_8), .out_3(steuerspeicher_8_out_3));
  assign out_18 = not_1_out ? steuerspeicher_8_out_3 : 1'bz;  // Controlled_Buffer controlled_buffer_8
endmodule
